# Fritzing sketch schematic (saved by Fritzing 0.9.3b)
stripboards: 1

parts:
  Part1 = Adafruit HUZZAH32 ESP32 Feather [part_number="Adafruit #3405"]
  Part2 = Mono 2.5W Class D Audio Amplifier - PAM8302
  SP1 = SPEAKER [package=pcb_mount_speaker]
  S1 = Reed switch [package=THT]

nets:
  N1: Part1.A5_IO4, S1.pin_2
  N2: Part1.A0_DAC2, Part2.AIN+
  GND: Part1.GND, Part2.GND, Part2.AIN-, S1.pin_1
  3.3V: Part1.3.3V, Part2.VCC
  N3: Part2.VO+, SP1.+
  N4: Part2.VO-, SP1.-

custom parts:
  Mono 2.5W Class D Audio Amplifier - PAM8302: A super small but powerful mono amplifier able to deliver up to 2.5 Watts into 4-8 ohm impedance speakers. Inside the miniature chip is a class D controller, able to run from 2.0V-5.5VDC. Since the amp is a class D, its very efficient (over 90% efficient when driving an 8Ω speaker at over half a Watt) - making it perfect for portable and battery-powered projects.
